# Fritzing sketch wiringDiagramBreakout (saved by Fritzing 0.9.3b)
breadboards: 1

parts:
  Part1 = Adafruit Feather M0 WINC1500 [part_number="Adafruit #3010"]
  Part2 = Adafruit RFM9x LoRa Radio [part_number="Adafruit #3072 and #3073"]

nets:
  N1: Part1.MISO, Part2.MISO
  N2: Part1.MOSI, Part2.MOSI
  N3: Part1.SCK, Part2.SCK
  GND: Part1.GND, Part2.GND
  +3V3: Part1.+3V3, Part2.VIN
  N4: Part1.D11, Part2.RST
  N5: Part1.D10, Part2.CS
  N6: Part1.D6, Part2.DIO0
  N7: Part2.DIO1, Part2.DIO2, Part2.DIO3, Part2.DIO4, Part2.DIO5

custom parts:
  Adafruit Feather M0 WINC1500: This is the Adafruit Feather M0 WiFi w/ATWINC1500 - our take on an 'all-in-one' Arduino-compatible + high speed, reliable WiFi with built in USB and battery charging. Its an Adafruit Feather M0 with a WiFi module, ready to rock! Connect your Feather to the Internet with this fine new FCC-certified WiFi module from Atmel. This 802.11bgn-capable WiFi module is the best new thing for networking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
  Adafruit RFM9x LoRa Radio: Sending data over long distances is like magic, and now you can be a magician with this range of powerful and easy-to-use radio modules. Sure, sometimes you want to talk to a computer (a good time to use WiFi) or perhaps communicate with a Phone (choose Bluetooth Low Energy!) but what if you want to send data very far? Most WiFi, Bluetooth, Zigbee and other wireless chipsets use 2.4GHz, which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
