# Fritzing sketch wiringDiagram (saved by Fritzing 0.9.3b)
breadboards: 1

parts:
  Part1 = Adafruit Feather 32u4 RFM69 433/900MHz [part_number="Adafruit #3076 and #3077"]
  R1 = Rotary Potentiometer (Small) [maximum_resistance=100kΩ package=THT]
  R2 = Rotary Potentiometer (Small) [maximum_resistance=100kΩ package=THT]
  R3 = Rotary Potentiometer (Small) [maximum_resistance=100kΩ package=THT]

nets:
  N1: Part1.A3, R3.wiper
  N2: Part1.A2, R2.wiper
  N3: Part1.A1, R1.wiper
  N4: Part1.A0, R1.leg1, R2.leg1, R3.leg1
  N5: Part1.GND, R1.leg2, R2.leg2, R3.leg2

custom parts:
  Adafruit Feather 32u4 RFM69 433/900MHz: This is the Adafruit Feather 32u4 Radio (RFM69HCW) - our take on an microcontroller packet radio transceiver with built in USB and battery charging. Its an Adafruit Feather 32u4 with a 433 or 900 MHz radio module cooked in! Great for making wireless networks that can go further than 2.4GHz 802.15.4 and similar, are more flexible than Bluetooth LE and without the high power requirements of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
